# Fritzing sketch DarthStep (saved by Fritzing 0.7.11b)
breadboards: 2

parts:
  U1 = Arduino Mega
  R1 = Rotary Potentiometer (Small) [maximum_resistance=10kΩ]
  R2 = Rotary Potentiometer (Small) [maximum_resistance=10kΩ]
  R3 = Photocell (LDR) [package=THT]
  R4 = Resistor [tolerance=±5% resistance=10k package=THT]
  DIN1 = DIN-5 jack (MIDI) [package=THT]
  R6 = Resistor [tolerance=±5% resistance=220 package=THT]
  R7 = Resistor [tolerance=±5% resistance=20k package=THT]
  R8 = Resistor [tolerance=±5% resistance=10k package=THT]
  R9 = Resistor [tolerance=±5% resistance=10k package=THT]
  R10 = Resistor [tolerance=±5% resistance=10k package=THT]
  R11 = Resistor [tolerance=±5% resistance=10k package=THT]
  R12 = Resistor [tolerance=±5% resistance=10k package=THT]
  R13 = Resistor [tolerance=±5% resistance=10k package=THT]
  R14 = Resistor [tolerance=±5% resistance=10k package=THT]
  R15 = Resistor [tolerance=±5% resistance=20k package=THT]
  R16 = Resistor [tolerance=±5% resistance=20k package=THT]
  R17 = Resistor [tolerance=±5% resistance=20k package=THT]
  R18 = Resistor [tolerance=±5% resistance=20k package=THT]
  R19 = Resistor [tolerance=±5% resistance=20k package=THT]
  R20 = Resistor [tolerance=±5% resistance=20k package=THT]
  R21 = Resistor [tolerance=±5% resistance=10k package=THT]
  R22 = Resistor [tolerance=±5% resistance=20k package=THT]
  R23 = Resistor [tolerance=±5% resistance=10k package=THT]
  IC1 = IC, DIP package, 8 pins [chip_label=LM386]
  R24 = Resistor [tolerance=±5% resistance=20k package=THT]
  C1 = Electrolytic Capacitor [capacitance=22µF voltage=35V package="100 mil [THT, electrolytic]"]
  C2 = Electrolytic Capacitor [capacitance=22µF voltage=35V package="100 mil [THT, electrolytic]"]
  R25 = Rotary Potentiometer (Small) [maximum_resistance=10kΩ]
  R26 = Resistor [tolerance=±5% resistance=4.7k package=THT]
  SPKR1 = Loudspeaker
  VCC1 = Battery block 9V
  U2 = 3-Axis Accelerometer Breakout

nets:
  GND: U1.GND, U1.VIN, R1.leg1, R2.leg2, R4.Pin_1, DIN1.2, R21.Pin_0, IC1.pin2, IC1.pin4, IC1.pin6, R25.leg2, R26.Pin_0, SPKR1.pin1, VCC1.-, VCC1.+, U2.GND
  +5V: U1.+5V, R1.leg2, R2.leg1, R3.pin_1, R6.Pin_0, U2.ST, U2.VDD
  N1: U1.A0, R7.Pin_1
  N2: U1.A1, R15.Pin_1
  N3: U1.A2, R16.Pin_1
  N4: U1.A3, R17.Pin_1
  N5: U1.A4, R18.Pin_1
  N6: U1.A5, R19.Pin_1
  N7: U1.D18, DIN1.5
  N8: U1.A6, R20.Pin_1
  N9: U1.A7, R22.Pin_1
  N10: U1.A8, R1.wiper
  N11: U1.A9, R2.wiper
  N12: U1.A10, R3.pin_0, R4.Pin_0
  N13: U1.A11, U2.X
  N14: U1.A13, U2.Y
  N15: U1.A14, U2.Z
  N16: DIN1.4, R6.Pin_1
  N17: R7.Pin_0, R8.Pin_1, R21.Pin_1
  N18: R8.Pin_0, R9.Pin_1, R15.Pin_0
  N19: R9.Pin_0, R10.Pin_1, R16.Pin_0
  N20: R10.Pin_0, R11.Pin_1, R17.Pin_0
  N21: R11.Pin_0, R12.Pin_1, R18.Pin_0
  N22: R12.Pin_0, R13.Pin_1, R19.Pin_0
  N23: R13.Pin_0, R14.Pin_1, R20.Pin_0
  N24: R14.Pin_0, R22.Pin_0, R23.Pin_1
  N25: R23.Pin_0, C1.+
  N26: IC1.pin3, R24.Pin_0, R26.Pin_1
  N27: IC1.pin5, C2.+
  N28: R24.Pin_1, C1.-
  N29: C2.-, R25.leg1
  N30: R25.wiper, SPKR1.pin2

notes:
  Pins 22 to 46 --> TFT
